# Fritzing sketch Rpi2_MotionDetector (saved by Fritzing 0.9.2b)

parts:
  PIR1 = PIR sensor
  Raspberry_Pi1 = Raspberry Pi 2

nets:
  VDD: PIR1.VDD, Raspberry_Pi1.5V
  N1: PIR1.SIG, Raspberry_Pi1.GPIO4
  GND: PIR1.GND, Raspberry_Pi1.GND
